// Logisim project Hager_FINAL_Stoplight_Project.circ as structural Verilog: 11 circuits, main circuit main
module main (
);

  wire and_1_out, and_2_out, clk, EN, G, G2, nState, PED_A, PED_B, ped_input_countdown_1_cycle_complete,
       ped_input_countdown_2_cycle_complete, R, R2, Y, Y2;
  wire [7:0] HEX0A, HEX0B, HEX1A, HEX1B;

  Clock u_clk (.out(clk));
  PED_Input_Countdown ped_input_countdown_1 (
    .allow_cross(R2), .PED_INPUT(PED_A), .HEX_1(HEX1A), .HEX_2(HEX0A),
    .Cycle_Complete(ped_input_countdown_1_cycle_complete));
  PED_Input_Countdown ped_input_countdown_2 (
    .allow_cross(R), .PED_INPUT(PED_B), .HEX_1(HEX1B), .HEX_2(HEX0B),
    .Cycle_Complete(ped_input_countdown_2_cycle_complete));
  FSM fsm_1 (.en(EN), .Next_State(clk), .G(G), .Y(Y), .R(R), .rst(nState), .G2(G2), .R2(R2), .Y2a(Y2));
  and and_1 (and_1_out, ped_input_countdown_1_cycle_complete, G);
  // RGBLED rgbled_1: pin names not known; wires that end beside it: R
  // RGBLED rgbled_2: pin names not known; wires that end beside it: Y, Y
  // RGBLED rgbled_3: pin names not known; wires that end beside it: G
  and and_2 (and_2_out, ped_input_countdown_2_cycle_complete, G2);
  Button u_PED_A (.out(PED_A));
  or or_1 (EN, Y, Y2, and_1_out, and_2_out);
  _7_Segment_Display #(.active("false")) u_7_segment_display_1 (
    .g(HEX1A[6]), .f(HEX1A[5]), .a(HEX1A[0]), .b(HEX1A[1]), .e(HEX1A[4]), .d(HEX1A[3]), .c(HEX1A[2]),
    .dp(HEX1A[7]));
  _7_Segment_Display #(.active("false")) u_7_segment_display_2 (
    .g(HEX0A[6]), .f(HEX0A[5]), .a(HEX0A[0]), .b(HEX0A[1]), .e(HEX0A[4]), .d(HEX0A[3]), .c(HEX0A[2]),
    .dp(HEX0A[7]));
  // RGBLED rgbled_4: pin names not known; wires that end beside it: R2
  // RGBLED rgbled_5: pin names not known; wires that end beside it: Y2, Y2
  // RGBLED rgbled_6: pin names not known; wires that end beside it: G2
  Button u_PED_B (.out(PED_B));
  _7_Segment_Display #(.active("false")) u_7_segment_display_3 (
    .g(HEX1B[6]), .f(HEX1B[5]), .a(HEX1B[0]), .b(HEX1B[1]), .e(HEX1B[4]), .d(HEX1B[3]), .c(HEX1B[2]),
    .dp(HEX1B[7]));
  _7_Segment_Display #(.active("false")) u_7_segment_display_4 (
    .g(HEX0B[6]), .f(HEX0B[5]), .a(HEX0B[0]), .b(HEX0B[1]), .e(HEX0B[4]), .d(HEX0B[3]), .c(HEX0B[2]),
    .dp(HEX0B[7]));

  // Notes on the sheet:
  //   Traffic Light A
  //   PED A IS REQUESTING TO CROSS VERTICALLY
  //   Counter Display
  //   Traffic Light B
  //   PED B IS REQUESTING TO CROSS HORIZONTALY
  //   Counter Display
endmodule

module Seg7_Decoder (
  input  i_m3,
  input  i_m2,
  input  i_m1,
  input  i_m0,
  output [7:0] o_seg
);

  wire and_1_out, and_2_out, and_3_out, and_4_out, and_5_out, and_6_out, and_7_out, and_8_out, and_9_out,
       and_10_out, and_11_out, and_12_out, and_13_out, and_14_out, and_15_out, and_16_out, and_17_out,
       and_18_out, and_19_out, and_20_out, and_21_out, and_22_out, and_23_out, not_1_out, not_2_out,
       not_3_out, not_4_out;

  not not_1 (not_1_out, i_m3);
  not not_2 (not_2_out, i_m2);
  not not_3 (not_3_out, i_m1);
  not not_4 (not_4_out, i_m0);
  and and_1 (and_1_out, not_1_out, not_2_out, not_3_out);
  and and_2 (and_2_out, not_1_out, i_m2, i_m1, i_m0);
  and and_3 (and_3_out, i_m3, not_2_out, i_m1);
  and and_4 (and_4_out, not_1_out, not_2_out, i_m0);
  and and_5 (and_5_out, not_1_out, not_2_out, i_m1);
  and and_6 (and_6_out, not_2_out, i_m1, i_m0);
  and and_7 (and_7_out, i_m3, i_m2, not_3_out);
  and and_8 (and_8_out, not_1_out, i_m2, not_3_out);
  and and_9 (and_9_out, i_m3, i_m2, i_m1);
  and and_10 (and_10_out, not_1_out, not_2_out, not_3_out, i_m0);
  and and_11 (and_11_out, not_1_out, i_m2, not_3_out, not_4_out);
  and and_12 (and_12_out, not_1_out, i_m2, i_m1, i_m0);
  and and_13 (and_13_out, i_m3, not_2_out, i_m1, i_m0);
  and and_14 (and_14_out, i_m3, i_m2, i_m1, not_4_out);
  and and_15 (and_15_out, not_1_out, not_2_out, i_m1, not_4_out);
  and and_16 (and_16_out, i_m3, i_m2, not_3_out, not_4_out);
  and and_17 (and_17_out, not_1_out, i_m2, not_3_out, i_m0);
  and and_18 (and_18_out, not_1_out, i_m2, i_m1, not_4_out);
  and and_19 (and_19_out, i_m3, i_m2, i_m1, i_m0);
  and and_20 (and_20_out, not_1_out, not_2_out, not_3_out, i_m0);
  and and_21 (and_21_out, not_1_out, i_m2, not_3_out, not_4_out);
  and and_22 (and_22_out, i_m3, not_2_out, i_m1, i_m0);
  and and_23 (and_23_out, i_m3, i_m2, i_m1, not_4_out);
  or or_1 (o_seg[6], and_1_out, and_2_out, and_3_out);
  or or_2 (o_seg[5], and_4_out, and_5_out, and_6_out, and_7_out);
  or or_3 (o_seg[4], i_m0, and_8_out, and_9_out);
  or or_4 (o_seg[3], and_10_out, and_11_out, and_12_out, and_13_out, and_14_out);
  or or_5 (o_seg[2], and_15_out, and_16_out);
  or or_6 (o_seg[1], and_17_out, and_18_out, and_19_out);
  or or_7 (o_seg[0], and_20_out, and_21_out, and_22_out, and_23_out);

  assign o_seg[7] = 1'b1;
endmodule

module CircuitA (
  input  i2,
  input  i1,
  input  i0,
  output o2,
  output o1,
  output o0
);

  not not_1 (o1, i1);
  and and_1 (o2, i2, i1);

  assign o0 = i0;
endmodule

module myComparator (
  input  v3,
  input  v2,
  input  v1,
  input  v0,
  output z
);

  wire and_1_out, and_2_out;

  and and_1 (and_1_out, v3, v1);
  and and_2 (and_2_out, v3, v2);
  or or_1 (z, and_1_out, and_2_out);
endmodule

module CircuitB (
  input  z,
  output s6,
  output s5,
  output s4,
  output s3,
  output s2,
  output s1,
  output s0
);


  assign s0 = z;
  assign s1 = 1'b0;
  assign s2 = 1'b0;
  assign s3 = z;
  assign s4 = z;
  assign s5 = z;
  assign s6 = 1'b1;
endmodule

module Bin2Hex (
  input  v3,
  input  v2,
  input  v1,
  input  v0,
  output [7:0] HEX1,
  output [7:0] HEX0
);

  wire z;

  myComparator myComparator_1 (.v3(v3), .v2(v2), .v1(v1), .v0(v0), .z(z));
  CircuitB CircuitB_1 (
    .z(z), .s6(HEX1[6]), .s5(HEX1[5]), .s4(HEX1[4]), .s3(HEX1[3]), .s2(HEX1[2]), .s1(HEX1[1]), .s0(HEX1[0]));
  Seg7_Decoder Seg7_Decoder_1 (.i_m3(v3), .i_m2(v2), .i_m1(v1), .i_m0(v0), .o_seg(HEX0));

  assign HEX1[7] = 1'b1;
endmodule

module pedestrian_button (
  input  [3:0] counter,
  output en
);

  or or_1 (en, counter[0], counter[1], counter[2], counter[3]);
endmodule

module DownCounter_v1 (
  input  en,
  output [3:0] count
);

  wire and_1_out, and_2_out, and_3_out, and_4_out, clock_1_out, t_ff_1_q, t_ff_2_q, t_ff_3_q;

  Clock clock_1 (.out(clock_1_out));
  T_Flip_Flop t_ff_1 (.T(en), .clk(clock_1_out), .Q(t_ff_1_q), .Qn(count[0]));  // open: reset, preset
  and and_1 (and_1_out, count[0], count[1], count[2], count[3]);
  and and_2 (and_2_out, en, t_ff_1_q);
  T_Flip_Flop t_ff_2 (.T(and_2_out), .clk(clock_1_out), .Q(t_ff_2_q), .Qn(count[1]));  // open: reset, preset
  and and_3 (and_3_out, and_2_out, t_ff_2_q);
  T_Flip_Flop t_ff_3 (
    .T(and_3_out), .clk(clock_1_out), .Q(t_ff_3_q), .Qn(count[2]), .preset(and_1_out));  // open: reset
  and and_4 (and_4_out, and_3_out, t_ff_3_q);
  T_Flip_Flop t_ff_4 (.T(and_4_out), .clk(clock_1_out), .Qn(count[3]), .preset(and_1_out));  // open: Q, reset

  // Notes on the sheet:
  //   Synchronous Down Counter from 3 to 0 with reset
endmodule

module FSM (
  input  en,
  input  Next_State,
  output G,
  output Y,
  output R,
  output rst,
  output G2,
  output R2,
  output Y2a
);

  wire and_3_out, and_4_out, and_6_out, and_7_out;
  wire [1:0] multiplexer_1_out, register_1_q;

  Multiplexer #(.select(3), .width(2)) multiplexer_1 (
    .in0(2'b00), .in1(2'b01), .in2(2'b10), .in3(2'b11), .in4(2'b01), .in5(2'b10), .in6(2'b11), .in7(2'b00),
    .out(multiplexer_1_out), .sel({en, register_1_q}));
  // Probe on multiplexer_1_out
  Register #(.width(2)) register_1 (.D(multiplexer_1_out), .Q(register_1_q), .clk(Next_State));  // open: en, clr
  // Probe on register_1_q
  and and_1 (G, ~register_1_q[0], ~register_1_q[1]);  // AND_Gate
  and and_2 (Y, register_1_q[0], ~register_1_q[1]);  // AND_Gate
  and and_3 (and_3_out, ~register_1_q[0], register_1_q[1]);  // AND_Gate
  and and_4 (and_4_out, register_1_q[0], register_1_q[1]);
  or or_1 (R, and_3_out, and_4_out);
  and and_5 (G2, ~register_1_q[0], register_1_q[1]);  // AND_Gate
  and and_6 (and_6_out, register_1_q[0], ~register_1_q[1]);  // AND_Gate
  and and_7 (and_7_out, ~register_1_q[0], ~register_1_q[1]);  // AND_Gate
  and and_8 (Y2a, register_1_q[1], register_1_q[0]);
  or or_2 (R2, and_6_out, and_7_out);

  assign rst = Next_State;
endmodule

module PED_Input_Countdown (
  input  allow_cross,
  input  PED_INPUT,
  output [7:0] HEX_1,
  output [7:0] HEX_2,
  output Cycle_Complete
);

  wire and_1_out, Clk, t_ff_1_q;
  wire [3:0] downcounter_10_clean_1_count_out;

  Clock clock_1 (.out(Clk));
  nor nor_1 (Cycle_Complete, downcounter_10_clean_1_count_out[0], downcounter_10_clean_1_count_out[1], downcounter_10_clean_1_count_out[2], downcounter_10_clean_1_count_out[3]);
  T_Flip_Flop t_ff_1 (.T(1'b1), .clk(Cycle_Complete), .Q(t_ff_1_q), .preset(PED_INPUT));  // open: Qn, reset
  and and_1 (and_1_out, allow_cross, t_ff_1_q);
  DownCounter_10_Clean downcounter_10_clean_1 (.en(and_1_out), .clk(Clk), .count_out(downcounter_10_clean_1_count_out));
  Bin2Hex bin2hex_1 (
    .v3(downcounter_10_clean_1_count_out[3]), .v2(downcounter_10_clean_1_count_out[2]),
    .v1(downcounter_10_clean_1_count_out[1]), .v0(downcounter_10_clean_1_count_out[0]), .HEX1(HEX_1),
    .HEX0(HEX_2));
endmodule

module DownCounter_10_Clean (
  input  en,
  input  clk,
  output [3:0] count_out
);

  wire and_2_out, not_1_out, not_2_out, not_3_out, not_4_out, not_5_out, not_6_out, T_Q1, T_Q2, T_Q3;

  not not_1 (not_1_out, count_out[0]);
  and and_1 (T_Q1, not_1_out, en);
  T_Flip_Flop Q0 (.T(en), .clk(clk), .Q(count_out[0]), .reset(and_2_out));  // open: Qn, preset
  and and_2 (and_2_out, count_out[0], count_out[1], count_out[2], count_out[3]);
  not not_2 (not_2_out, count_out[0]);
  not not_3 (not_3_out, count_out[1]);
  T_Flip_Flop Q1 (.T(T_Q1), .clk(clk), .Q(count_out[1]));  // open: Qn, reset, preset
  and and_3 (T_Q2, not_2_out, not_3_out, en);
  T_Flip_Flop Q2 (.T(T_Q2), .clk(clk), .Q(count_out[2]), .reset(and_2_out));  // open: Qn, preset
  not not_4 (not_4_out, count_out[0]);
  not not_5 (not_5_out, count_out[1]);
  not not_6 (not_6_out, count_out[2]);
  T_Flip_Flop Q3 (.T(T_Q3), .clk(clk), .Q(count_out[3]));  // open: Qn, reset, preset
  and and_4 (T_Q3, not_4_out, not_5_out, not_6_out, en);

  // Other names for the same wires on the sheet: Q_A = count_out[0]; Q_B = count_out[1]; Q_C = count_out[2];
  //   Q_D = count_out[3]
endmodule
