// Logisim project 02Lab_Full_Adder.circ as structural Verilog: 2 circuits, main circuit Half_Add
module Half_Add (
  input  Input_1,
  input  Input_2,
  output Output_1,
  output Output_2
);

  and and_1 (Output_2, Input_1, Input_2);
  xor xor_1 (Output_1, Input_1, Input_2);
endmodule

module Full_Add (
  input  Input_1,
  input  Input_2,
  input  Input_3,
  output Output_1,
  output Output_2
);

  wire Half_Add_1_output_1, Half_Add_1_output_2, Half_Add_2_output_1;

  Half_Add Half_Add_1 (
    .Input_1(Input_2), .Input_2(Input_3), .Output_1(Half_Add_1_output_1), .Output_2(Half_Add_1_output_2));
  Half_Add Half_Add_2 (
    .Input_1(Half_Add_1_output_2), .Input_2(Input_1), .Output_1(Half_Add_2_output_1), .Output_2(Output_2));
  or or_1 (Output_1, Half_Add_1_output_1, Half_Add_2_output_1);

  // Other names for the same wires on the sheet: A = Input_2; B = Input_3; Cin = Input_1
endmodule
