// Logisim project FA_MUX_Decoder_Activity.circ as structural Verilog: 4 circuits, main circuit main
module main (
  input  Cin,
  input  A,
  input  B,
  input  s,
  output count,
  output sum,
  output mode
);

  wire count0, count1, sum0, sum1;

  MUX_FA MUX_FA_1 (.Input_1(Cin), .Input_2(A), .Input_3(B), .count(count0), .sum(sum0));
  DECODER_FA decoder_fa_1 (.Input_1(Cin), .Input_2(A), .Input_3(B), .count_d(count1), .sum(sum1));
  Multiplexer multiplexer_1 (.in0(count0), .in1(count1), .out(count), .sel(s));
  Multiplexer multiplexer_2 (.in0(sum0), .in1(sum1), .out(sum), .sel(s));

  assign mode = s;
endmodule

module MUX_FA (
  input  Input_1,
  input  Input_2,
  input  Input_3,
  output count,
  output sum
);

  Multiplexer #(.select(3)) multiplexer_1 (
    .in0(1'b0), .in1(1'b0), .in2(1'b0), .in3(1'b1), .in4(1'b0), .in5(1'b1), .in6(1'b1), .in7(1'b1),
    .out(count), .sel({Input_2, Input_1, Input_3}));
  Multiplexer #(.select(3)) multiplexer_2 (
    .in0(1'b0), .in1(1'b1), .in2(1'b1), .in3(1'b0), .in4(1'b1), .in5(1'b0), .in6(1'b0), .in7(1'b1),
    .out(sum), .sel({Input_2, Input_1, Input_3}));

  // Other names for the same wires on the sheet: c_in = Input_3; A = Input_1; B = Input_2
endmodule

module DECODER_FA (
  input  Input_1,
  input  Input_2,
  input  Input_3,
  output count_d,
  output sum
);

  wire decoder_1_out3, decoder_1_out5, decoder_1_out6, decoder_1_out7, decoder_2_out1, decoder_2_out2,
       decoder_2_out4, decoder_2_out7;

  Decoder #(.select(3)) decoder_1 (
    .out3(decoder_1_out3), .out5(decoder_1_out5), .out6(decoder_1_out6), .out7(decoder_1_out7),
    .sel({Input_2, Input_1, Input_3}));  // open: out0, out1, out2, out4, en
  or or_1 (count_d, decoder_1_out3, decoder_1_out5, decoder_1_out6, decoder_1_out7);
  Decoder #(.select(3)) decoder_2 (
    .out1(decoder_2_out1), .out2(decoder_2_out2), .out4(decoder_2_out4), .out7(decoder_2_out7),
    .sel({Input_2, Input_1, Input_3}));  // open: out0, out3, out5, out6, en
  or or_2 (sum, decoder_2_out1, decoder_2_out2, decoder_2_out4, decoder_2_out7);

  // Other names for the same wires on the sheet: c_in = Input_3; A = Input_1; B = Input_2

  // Notes on the sheet:
  //   m(3,5,6,7)
  //   m(1,2,4,7)
endmodule

module DECODER_FA_TEST (
  input  A,
  input  B,
  input  c_in,
  output count,
  output sum
);

  DECODER_FA MUX_decoder_1 (.Input_1(A), .Input_2(B), .Input_3(c_in), .count_d(count), .sum(sum));
endmodule
