// Logisim project 10_RGB_LED.circ as structural Verilog: 4 circuits, main circuit main
module main (
  input  Input_1,
  input  Input_2,
  input  Input_3,
  output Output_1,
  output Output_2,
  output Output_3
);

  wire G_Clk, LED2, LED2_a, LED3_a;

  All_Color_Cycle All_Color_Cycle_1 (.Input_1(Input_1), .Output_3({G_Clk, LED2, Output_1}));
  Red_Blink_Cycle Red_Blink_Cycle_1 (.Clk1(Input_2), .Input_1(Output_1), .Output_1(LED3_a));
  Green_Blink_Cycle Green_Blink_Cycle_1 (.clk2(Input_3), .Input_1(G_Clk), .Output_1(LED2_a));
  or or_1 (Output_2, LED2, LED2_a);
  or or_2 (Output_3, G_Clk, LED3_a);

  // Other names for the same wires on the sheet: LED1 = Output_1; R_Clk = Output_1; LED3 = G_Clk
endmodule

module All_Color_Cycle (
  input  Input_1,
  output [2:0] Output_3
);

  wire and_1_out, clock_1_out, not_1_out;

  Counter #(.max('h7), .width(3)) counter_1 (
    .Q(Output_3), .clk(and_1_out), .clr(not_1_out));  // open: load, D, count, carry, up
  not not_1 (not_1_out, Input_1);
  and and_1 (and_1_out, Input_1, clock_1_out);
  Clock clock_1 (.out(clock_1_out));
endmodule

module Red_Blink_Cycle (
  input  Clk1,
  input  Input_1,
  output Output_1
);

  and and_1 (Output_1, Clk1, Input_1);
endmodule

module Green_Blink_Cycle (
  input  clk2,
  input  Input_1,
  output Output_1
);

  and and_1 (Output_1, clk2, Input_1);
endmodule
